# Fritzing sketch Basic Digital and Analog IO Board (saved by Fritzing 1.0.6)
breadboards: 1

parts:
  LED1 = LED - 5mm [color="Red (633nm)" current=0.030A package="5 mm [THT]"]
  Bauteil1 = Arduino Uno (Rev3)
  R4 = Resistor [tolerance=±5% power=0.25W resistance=220 package=THT]
  S1 = Pushbutton [package="[THT]"]
  R5 = Rotary Potentiometer (Small) [maximum_resistance=10kΩ knob_status=50% power=0.5W package=THT]
  R6 = Resistor [tolerance=±5% power=0.25W resistance=1k package=THT]
  R7 = Resistor [tolerance=±5% power=0.25W resistance=1k package=THT]

nets:
  N1: LED1.cathode, R4.Pin_1
  N2: LED1.anode, Bauteil1.5V, R5.leg1
  N3: Bauteil1.A0, R7.Pin_1
  N4: Bauteil1.D8, R6.Pin_0
  N5: Bauteil1.D11_PWM/MOSI, R4.Pin_0
  N6: Bauteil1.GND, S1.Pin_1, S1.Pin_2, R5.leg2
  N7: S1.Pin_3, S1.Pin_4, R6.Pin_1
  N8: R5.wiper, R7.Pin_0
