# Fritzing sketch Digital IO Batterytester (saved by Fritzing 1.0.6)
breadboards: 1

parts:
  R2 = Resistor [tolerance=±5% power=0.25W resistance=220 package=THT]
  LED1 = LED - 5mm [color="Red (633nm)" current=0.030A package="5 mm [THT]"]
  LED2 = LED - 5mm [color="Yellow (595nm)" current=0.030A package="5 mm [THT]"]
  LED3 = LED - 5mm [color="Green (570nm)" current=0.030A package="5 mm [THT]"]
  Bauteil1 = Arduino Uno (Rev3)
  R3 = Resistor [tolerance=±5% power=0.25W resistance=220 package=THT]
  R4 = Resistor [tolerance=±5% power=0.25W resistance=220 package=THT]
  BAT1 = Battery Holders [package=battery-aa]

nets:
  N1: R2.Pin_0, Bauteil1.D9_PWM
  N2: R2.Pin_1, LED3.cathode
  N3: LED1.cathode, R4.Pin_1
  N4: LED1.anode, LED2.anode, LED3.anode, Bauteil1.5V
  N5: LED2.cathode, R3.Pin_1
  N6: Bauteil1.A0, BAT1.+
  N7: Bauteil1.D10_PWM/SS, R3.Pin_0
  N8: Bauteil1.D11_PWM/MOSI, R4.Pin_0
  N9: Bauteil1.GND, BAT1.-
