# Fritzing sketch Wuerfel Board Schaltplan (saved by Fritzing 1.0.6)
breadboards: 1

parts:
  LED1 = LED - 5mm [color="Red (633nm)" current=0.030A package="5 mm [THT]"]
  LED2 = LED - 5mm [color="Red (633nm)" current=0.030A package="5 mm [THT]"]
  LED3 = LED - 5mm [color="Red (633nm)" current=0.030A package="5 mm [THT]"]
  LED4 = LED - 5mm [color="Red (633nm)" current=0.030A package="5 mm [THT]"]
  LED5 = LED - 5mm [color="Red (633nm)" current=0.030A package="5 mm [THT]"]
  LED6 = LED - 5mm [color="Red (633nm)" current=0.030A package="5 mm [THT]"]
  LED7 = LED - 5mm [color="Red (633nm)" current=0.030A package="5 mm [THT]"]
  S1 = Pushbutton [package="[THT]"]
  R2 = Resistor [tolerance=±5% power=0.25W resistance=220 package=THT]
  R3 = Resistor [tolerance=±5% power=0.25W resistance=220 package=THT]
  R4 = Resistor [tolerance=±5% power=0.25W resistance=220 package=THT]
  R5 = Resistor [tolerance=±5% power=0.25W resistance=220 package=THT]
  R6 = Resistor [tolerance=±5% power=0.25W resistance=220 package=THT]
  R7 = Resistor [tolerance=±5% power=0.25W resistance=220 package=THT]
  R8 = Resistor [tolerance=±5% power=0.25W resistance=220 package=THT]
  R9 = Resistor [tolerance=±5% power=0.25W resistance=220 package=THT]
  Bauteil1 = Arduino Uno (Rev3)

nets:
  N1: LED1.cathode, R3.Pin_1
  N2: LED1.anode, LED2.anode, LED3.anode, R5.Pin_0, R6.Pin_1, R7.Pin_1, R8.Pin_1, Bauteil1.5V
  N3: LED2.cathode, R4.Pin_1
  N4: LED3.cathode, R2.Pin_1
  N5: LED4.cathode, Bauteil1.D11_PWM/MOSI
  N6: LED4.anode, R5.Pin_1
  N7: LED5.cathode, Bauteil1.D2
  N8: LED5.anode, R8.Pin_0
  N9: LED6.cathode, Bauteil1.D4
  N10: LED6.anode, R7.Pin_0
  N11: LED7.cathode, Bauteil1.D6_PWM
  N12: LED7.anode, R6.Pin_0
  N13: S1.Pin_1, S1.Pin_2, R9.Pin_0
  N14: S1.Pin_3, S1.Pin_4, Bauteil1.D8
  N15: R2.Pin_0, Bauteil1.D7
  N16: R3.Pin_0, Bauteil1.D3_PWM
  N17: R4.Pin_0, Bauteil1.D5_PWM
  0V: R9.Pin_1, Bauteil1.GND
